# Fritzing sketch arduino_eq1 (saved by Fritzing 0.9.3b)
breadboards: 1

parts:
  Componente1 = Arduino Nano (Rev3.0)
  Pololu_A1 = Pololu A4988 [package=SO16]
  M2 = Stepper Motor - Bipolar

nets:
  N1: Componente1.D3, Pololu_A1.STEP
  N2: Componente1.D4, Pololu_A1.DIR
  N3: Componente1.D5, Pololu_A1.ENABLE
  N4: Pololu_A1.MS1, Pololu_A1.MS2, Pololu_A1.MS3, Pololu_A1.RESET, Pololu_A1.SLEEP, Pololu_A1.VDD
  N5: Pololu_A1.1B, M2.D
  N6: Pololu_A1.1A, M2.B
  N7: Pololu_A1.2A, M2.C
  N8: Pololu_A1.2B, M2.A
